// Logisim project main.circ as structural Verilog: 7 circuits, main circuit main
module main (
  input  in_1,
  input  in_2,
  output [15:0] out_3,
  output [15:0] DATA_BUS_STATUS,
  output [15:0] RAM_STATUS,
  output [15:0] STACK_STATUS,
  output [15:0] out_7,
  output [15:0] ALU_STATUS,
  output [7:0] out_9,
  output [3:0] out_10,
  output [15:0] out_11,
  output [2:0] out_12,
  output [15:0] out_13
);

  wire ALU_SRC, and_1_out, and_2_out, and_3_out, and_4_out, and_5_out, and_6_out, CLOCK, clock_1_out,
       comparator_1_eq, comparator_1_gt, comparator_1_lt, HALT, I_O_SRC, INC_PC, JNEG, JPOS, JZ, not_1_out,
       not_2_out, not_3_out, OPERAND_SRC, or_2_out, PC_ADRESS_WRITE, PC_SRC, RAM_SRC, STACK_NEXT_SRC,
       STACK_POP, STACK_TOP_SRC, t_ff_1_q, t_ff_1_qn, t_ff_2_q, t_ff_2_qn;
  wire [11:4] controlled_buffer_7_out;
  wire [15:0] controlled_buffer_1_out;

  assign controlled_buffer_1_out = out_9[6] ? STACK_STATUS : 16'bz;  // Controlled_Buffer controlled_buffer_1
  assign controlled_buffer_1_out = ~out_9[6] ? DATA_BUS_STATUS : 16'bz;  // Controlled_Buffer controlled_buffer_2
  Clock clock_1 (.out(clock_1_out));
  and and_1 (and_1_out, ~out_9[6], out_9[4]);  // AND_Gate
  and and_2 (and_2_out, out_9[6], out_9[4], or_2_out);
  or or_1 (PC_ADRESS_WRITE, and_1_out, and_2_out);
  and and_3 (and_3_out, clock_1_out, ~HALT, ~in_2);  // AND_Gate
  LED led_1 (.in(in_2));
  Comparator #(.width(16)) comparator_1 (
    .a(out_11), .b({16{1'b0}}), .gt(comparator_1_gt), .eq(comparator_1_eq), .lt(comparator_1_lt));
  or or_2 (or_2_out, and_4_out, and_5_out, and_6_out);
  Counter #(.width(16), .max('hffff), .ongoal("stay")) PC (
    .load(PC_ADRESS_WRITE), .D(controlled_buffer_1_out), .Q(out_13), .clk(INC_PC));  // open: count, carry, clr, preset, down
  not not_1 (not_1_out, and_3_out);
  and and_4 (and_4_out, comparator_1_gt, JPOS);
  and and_5 (and_5_out, comparator_1_eq, JZ);
  T_Flip_Flop t_ff_1 (.clk(not_1_out), .T(1'b1), .Q(t_ff_1_q), .Qn(t_ff_1_qn));  // open: preset, reset
  T_Flip_Flop #(.Pre_Clr_Positions("LEGACY"), .enable("true")) t_ff_2 (
    .clk(and_3_out), .T(1'b1), .Q(t_ff_2_q), .Qn(t_ff_2_qn));  // open: preset, reset, en
  and and_6 (and_6_out, comparator_1_lt, JNEG);
  and and_7 (CLOCK, and_3_out, t_ff_1_qn, t_ff_2_q);
  and and_8 (INC_PC, t_ff_2_qn, t_ff_1_q, and_3_out);
  assign DATA_BUS_STATUS = PC_SRC ? out_13 : 16'bz;  // Controlled_Buffer controlled_buffer_3
  assign DATA_BUS_STATUS = OPERAND_SRC ? out_7 : 16'bz;  // Controlled_Buffer controlled_buffer_4
  ROM #(.addrWidth(16), .dataWidth(24), .Select("low")) Program (.addr(out_13), .data({out_9, out_7}));
  not not_2 (not_2_out, out_9[5]);
  RAM #(.addrWidth(16), .dataWidth(16), .Select("low")) DATA (
    .addr(STACK_STATUS), .data(DATA_BUS_STATUS), .sel(not_2_out), .clk(CLOCK), .ld(RAM_SRC));  // open: clr
  // Probe on out_13
  LED led_2 (.in(PC_ADRESS_WRITE));
  stack stack_1 (
    .IN(DATA_BUS_STATUS), .PUSH(out_9[7]), .POP(STACK_POP), .SEL(in_1), .CLOCK(CLOCK), .TOP(STACK_STATUS),
    .NEXT(out_11));  // open: SWAP, HAS_NEXT, OVERFLOW
  Decoder #(.select(3), .enable("false")) decoder_1 (
    .out0(OPERAND_SRC), .out1(RAM_SRC), .out2(ALU_SRC), .out3(I_O_SRC), .out4(PC_SRC), .out5(STACK_TOP_SRC),
    .out6(STACK_NEXT_SRC), .sel(out_9[2:0]));  // open: out7
  assign DATA_BUS_STATUS = STACK_NEXT_SRC ? out_11 : 16'bz;  // Controlled_Buffer controlled_buffer_5
  assign DATA_BUS_STATUS = STACK_TOP_SRC ? STACK_STATUS : 16'bz;  // Controlled_Buffer controlled_buffer_6
  not not_3 (not_3_out, out_9[6]);
  assign {STACK_POP, JZ, JNEG, JPOS, controlled_buffer_7_out, out_10} = out_9[6] ? out_7 : 16'bz;  // Controlled_Buffer controlled_buffer_7
  assign {STACK_POP, JZ, JNEG, JPOS, controlled_buffer_7_out, out_10} = not_3_out ? {16{1'b0}} : 16'bz;  // Controlled_Buffer controlled_buffer_8
  alu alu_1 (.A(STACK_STATUS), .B(out_11), .ALU_OP(out_10), .OUT(ALU_STATUS));  // open: CARRY_IN, ZF, CF
  assign DATA_BUS_STATUS = ALU_SRC ? ALU_STATUS : 16'bz;  // Controlled_Buffer controlled_buffer_9
  nor nor_1 (HALT, out_9[0], out_9[1], out_9[2], out_9[3], out_9[4], out_9[5], out_9[6], out_9[7]);
  assign DATA_BUS_STATUS = I_O_SRC ? {16{1'b1}} : 16'bz;  // Controlled_Buffer controlled_buffer_10

  assign out_3 = {16{1'b1}};
  assign out_12 = out_9[2:0];

  // Other names for the same wires on the sheet: ARGUMENT[15:0] = out_7; OPCODE[7:0] = out_9; SRC[2:0] = out_9[2:0];
  //   PC = out_9[4]; RAM = out_9[5]; _24BIT_INSTUCTION = out_9[6]; STACK_PUSH = out_9[7]; ALU_OP[3:0] = out_10;
  //   ALU_OUT[15:0] = ALU_STATUS; BADOP = in_2; DATA_BUS[15:0] = DATA_BUS_STATUS; PROGRAM_COUNTER[15:0] = out_13;
  //   RAM_VALUE[15:0] = RAM_STATUS; STACK_NEXT[15:0] = out_11; STACK_TOP[15:0] = STACK_STATUS

  // Notes on the sheet:
  //   Main architecture
  //   CLOCK
  //   PROGRAM COUNTER
  //   Conditional jumps
  //   ROM
  //   contents of Program (hex, n*v repeats v):
  //   80ffff 800000 800000 408000 408000 408000 100000
  //   COMPUTER STATUS
  //   INSTRUCTION STATUS
  //   RAM
  //   PC STATUS
  //   STACK
  //   SOURCE DECODER
  //   DECODER
  //   ALU
  //   HALT
  //   I/O
endmodule

// ALU
module alu (
  input  [15:0] A,
  input  [15:0] B,
  input  [3:0] ALU_OP,
  input  CARRY_IN,
  output [15:0] OUT,
  output ZF,
  output CF
);

  wire [15:0] adder_1_out, adder_2_out, and_1_out, nand_1_out, negator_1_out, nor_1_out, not_1_out, or_1_out,
       subtractor_1_out, subtractor_2_out, xor_1_out;

  Adder #(.width(16)) adder_1 (.a(A), .b(B), .out(adder_1_out));  // open: cin, cout
  Adder #(.width(16)) adder_2 (.a(A), .b(B), .out(adder_2_out), .cin(CARRY_IN));  // open: cout
  Subtractor #(.width(16)) subtractor_1 (.a(A), .b(B), .out(subtractor_1_out));  // open: bin, bout
  Subtractor #(.width(16)) subtractor_2 (.a(A), .b(B), .out(subtractor_2_out), .bin(CARRY_IN));  // open: bout
  Comparator #(.width(16)) comparator_1 (.a(A), .b(B), .eq(ZF), .lt(CF));  // open: gt
  Negator #(.width(16)) negator_1 (.in(A), .out(negator_1_out));
  assign not_1_out = ~A;  // NOT_Gate not_1, 16 bits wide
  assign and_1_out = A & B;  // AND_Gate and_1, 16 bits wide
  assign or_1_out = A | B;  // OR_Gate or_1, 16 bits wide
  assign nand_1_out = ~(A & B);  // NAND_Gate nand_1, 16 bits wide
  assign nor_1_out = ~(A | B);  // NOR_Gate nor_1, 16 bits wide
  assign xor_1_out = A ^ B;  // XOR_Gate xor_1, 16 bits wide
  Multiplexer #(.select(4), .width(16), .enable("false")) multiplexer_1 (
    .in0(adder_1_out), .in1(adder_2_out), .in2(subtractor_1_out), .in3(subtractor_2_out),
    .in4(negator_1_out), .in5(not_1_out), .in6(and_1_out), .in7(or_1_out), .in8(nand_1_out), .in9(nor_1_out),
    .in10(xor_1_out), .out(OUT), .sel(ALU_OP));  // open: in11, in12, in13, in14, in15

  // Notes on the sheet:
  //   ALU interface
endmodule

// STACK
module stack (
  input  [15:0] IN,
  input  SWAP,
  input  PUSH,
  input  POP,
  input  SEL,
  input  CLOCK,
  output [15:0] TOP,
  output [15:0] NEXT,
  output HAS_NEXT,
  output OVERFLOW
);

  wire decoder_1_out0, decoder_1_out1, decoder_1_out2, decoder_1_out3, decoder_1_out4, decoder_1_out5,
       decoder_1_out6, decoder_1_out7, decoder_1_out8, decoder_1_out9, decoder_1_out10, decoder_1_out11,
       decoder_1_out12, decoder_1_out13, decoder_1_out14, decoder_1_out15, decoder_1_out16, decoder_1_out17,
       decoder_1_out18, decoder_1_out19, decoder_1_out20, decoder_1_out21, decoder_1_out22, decoder_1_out23,
       decoder_1_out24, decoder_1_out25, decoder_1_out26, decoder_1_out27, decoder_1_out28, decoder_1_out29,
       decoder_1_out30, decoder_1_out31, decoder_2_out0, decoder_2_out1, decoder_2_out2, decoder_2_out3,
       decoder_2_out4, decoder_2_out5, decoder_2_out6, decoder_2_out7, decoder_2_out8, decoder_2_out9,
       decoder_2_out10, decoder_2_out11, decoder_2_out12, decoder_2_out13, decoder_2_out14, decoder_2_out16,
       decoder_2_out17, decoder_2_out18, decoder_2_out19, decoder_2_out20, decoder_2_out21, decoder_2_out22,
       decoder_2_out23, decoder_2_out24, decoder_2_out25, decoder_2_out26, decoder_2_out27, decoder_2_out28,
       decoder_2_out29, decoder_2_out30, decoder_2_out31, or_1_out;
  wire [4:0] adder_1_out, multiplexer_1_out, subtractor_1_out, subtractor_2_out, subtractor_3_out,
       subtractor_4_out, subtractor_5_out, TOP_PTR_q;
  wire [15:0] _1, sut4_1_out_1, sut4_1_out_2, sut4_1_out_3, sut4_1_out_4, sut4_1_out_5, sut4_1_out_6,
       sut4_1_out_7, sut4_1_out_8, sut4_1_out_9, sut4_1_out_10, sut4_1_out_11, sut4_1_out_12, sut4_1_out_13,
       sut4_1_out_14, sut4_1_out_15, sut4_1_out_16, sut4_2_out_2, sut4_2_out_3, sut4_2_out_4, sut4_2_out_5,
       sut4_2_out_6, sut4_2_out_7, sut4_2_out_8, sut4_2_out_9, sut4_2_out_10, sut4_2_out_11, sut4_2_out_13,
       sut4_2_out_14, sut4_2_out_15, sut4_2_out_16;

  Subtractor #(.width(5)) subtractor_1 (.a(TOP_PTR_q), .b({4'b0000, SWAP}), .out(subtractor_1_out));  // open: bin, bout
  Decoder #(.select(5), .enable("false")) decoder_1 (
    .out0(decoder_1_out0), .out1(decoder_1_out1), .out2(decoder_1_out2), .out3(decoder_1_out3),
    .out4(decoder_1_out4), .out5(decoder_1_out5), .out6(decoder_1_out6), .out7(decoder_1_out7),
    .out8(decoder_1_out8), .out9(decoder_1_out9), .out10(decoder_1_out10), .out11(decoder_1_out11),
    .out12(decoder_1_out12), .out13(decoder_1_out13), .out14(decoder_1_out14), .out15(decoder_1_out15),
    .out16(decoder_1_out16), .out17(decoder_1_out17), .out18(decoder_1_out18), .out19(decoder_1_out19),
    .out20(decoder_1_out20), .out21(decoder_1_out21), .out22(decoder_1_out22), .out23(decoder_1_out23),
    .out24(decoder_1_out24), .out25(decoder_1_out25), .out26(decoder_1_out26), .out27(decoder_1_out27),
    .out28(decoder_1_out28), .out29(decoder_1_out29), .out30(decoder_1_out30), .out31(decoder_1_out31),
    .sel(subtractor_2_out));
  Subtractor #(.width(5)) subtractor_2 (.a(subtractor_1_out), .b(5'b00001), .out(subtractor_2_out));  // open: bin, bout
  Decoder #(.select(5), .enable("false")) decoder_2 (
    .out0(decoder_2_out0), .out1(decoder_2_out1), .out2(decoder_2_out2), .out3(decoder_2_out3),
    .out4(decoder_2_out4), .out5(decoder_2_out5), .out6(decoder_2_out6), .out7(decoder_2_out7),
    .out8(decoder_2_out8), .out9(decoder_2_out9), .out10(decoder_2_out10), .out11(decoder_2_out11),
    .out12(decoder_2_out12), .out13(decoder_2_out13), .out14(decoder_2_out14), .out15(decoder_2_out14),
    .out16(decoder_2_out16), .out17(decoder_2_out17), .out18(decoder_2_out18), .out19(decoder_2_out19),
    .out20(decoder_2_out20), .out21(decoder_2_out21), .out22(decoder_2_out22), .out23(decoder_2_out23),
    .out24(decoder_2_out24), .out25(decoder_2_out25), .out26(decoder_2_out26), .out27(decoder_2_out27),
    .out28(decoder_2_out28), .out29(decoder_2_out29), .out30(decoder_2_out30), .out31(decoder_2_out31),
    .sel(subtractor_1_out));
  sut4 sut4_1 (
    .NEXT(NEXT), .TOP(TOP), .IS_NEXT_1(decoder_1_out0), .EN_1(decoder_2_out0), .IS_NEXT_2(decoder_1_out1),
    .IN(IN), .EN_2(decoder_2_out1), .IS_NEXT_3(decoder_1_out2), .EN_3(decoder_2_out2),
    .IS_NEXT_4(decoder_1_out3), .EN_4(decoder_2_out3), .SWAP(SWAP), .CLOCK(CLOCK),
    .IS_NEXT_5(decoder_1_out4), .EN_5(decoder_2_out4), .IS_NEXT_6(decoder_1_out5), .SEL(SEL),
    .EN_6(decoder_2_out5), .IS_NEXT_7(decoder_1_out6), .EN_7(decoder_2_out6), .IS_NEXT_8(decoder_1_out7),
    .EN_8(decoder_2_out7), .IS_NEXT_9(decoder_1_out8), .EN_9(decoder_2_out8), .IS_NEXT_10(decoder_1_out9),
    .EN_10(decoder_2_out9), .IS_NEXT_11(decoder_1_out10), .EN_11(decoder_2_out10),
    .IS_NEXT_12(decoder_1_out11), .EN_12(decoder_2_out11), .IS_NEXT_13(decoder_1_out12),
    .EN_13(decoder_2_out12), .IS_NEXT_14(decoder_1_out13), .EN_14(decoder_2_out13),
    .IS_NEXT_15(decoder_1_out14), .IS_NEXT_16(decoder_1_out15), .OUT_1(sut4_1_out_1), .OUT_2(sut4_1_out_2),
    .OUT_3(sut4_1_out_3), .OUT_4(sut4_1_out_4), .OUT_5(sut4_1_out_5), .OUT_6(sut4_1_out_6),
    .OUT_7(sut4_1_out_7), .OUT_8(sut4_1_out_8), .OUT_9(sut4_1_out_9), .OUT_10(sut4_1_out_10),
    .OUT_11(sut4_1_out_11), .OUT_12(sut4_1_out_12), .OUT_13(sut4_1_out_13), .OUT_14(sut4_1_out_14),
    .OUT_15(sut4_1_out_15), .OUT_16(sut4_1_out_16));  // open: EN_15, EN_16
  sut4 sut4_2 (
    .NEXT(NEXT), .TOP(TOP), .IS_NEXT_1(decoder_1_out16), .EN_1(decoder_2_out16), .IS_NEXT_2(decoder_1_out17),
    .IN(IN), .EN_2(decoder_2_out17), .IS_NEXT_3(decoder_1_out18), .EN_3(decoder_2_out18),
    .IS_NEXT_4(decoder_1_out19), .EN_4(decoder_2_out19), .SWAP(SWAP), .CLOCK(CLOCK),
    .IS_NEXT_5(decoder_1_out20), .EN_5(decoder_2_out20), .IS_NEXT_6(decoder_1_out21), .SEL(SEL),
    .EN_6(decoder_2_out21), .IS_NEXT_7(decoder_1_out22), .EN_7(decoder_2_out22), .IS_NEXT_8(decoder_1_out23),
    .EN_8(decoder_2_out23), .IS_NEXT_9(decoder_1_out24), .EN_9(decoder_2_out24),
    .IS_NEXT_10(decoder_1_out25), .EN_10(decoder_2_out25), .IS_NEXT_11(decoder_1_out26),
    .EN_11(decoder_2_out26), .IS_NEXT_12(decoder_1_out27), .EN_12(decoder_2_out27),
    .IS_NEXT_13(decoder_1_out28), .EN_13(decoder_2_out28), .IS_NEXT_14(decoder_1_out29),
    .EN_14(decoder_2_out29), .IS_NEXT_15(decoder_1_out30), .EN_15(decoder_2_out30),
    .IS_NEXT_16(decoder_1_out31), .EN_16(decoder_2_out31), .OUT_1(_1), .OUT_2(sut4_2_out_2),
    .OUT_3(sut4_2_out_3), .OUT_4(sut4_2_out_4), .OUT_5(sut4_2_out_5), .OUT_6(sut4_2_out_6),
    .OUT_7(sut4_2_out_7), .OUT_8(sut4_2_out_8), .OUT_9(sut4_2_out_9), .OUT_10(sut4_2_out_10),
    .OUT_11(sut4_2_out_11), .OUT_12(sut4_2_out_11), .OUT_13(sut4_2_out_13), .OUT_14(sut4_2_out_14),
    .OUT_15(sut4_2_out_15), .OUT_16(sut4_2_out_16));
  Subtractor #(.width(5)) subtractor_3 (.a(TOP_PTR_q), .b(5'b00001), .out(subtractor_3_out));  // open: bin, bout
  Adder #(.width(5)) adder_1 (.a(TOP_PTR_q), .b(5'b00001), .out(adder_1_out));  // open: cin, cout
  Multiplexer #(.width(5), .enable("false")) multiplexer_1 (
    .in0(subtractor_3_out), .in1(adder_1_out), .out(multiplexer_1_out), .sel(PUSH));
  Register #(.width(5), .Select("low")) TOP_PTR (
    .D(multiplexer_1_out), .en(or_1_out), .Q(TOP_PTR_q), .clk(CLOCK));  // open: clr
  or or_1 (or_1_out, PUSH, POP);
  Comparator #(.width(5), .mode("unsigned")) comparator_1 (
    .a(TOP_PTR_q), .b({5{1'b1}}), .gt(OVERFLOW));  // open: eq, lt
  Comparator #(.width(5), .mode("unsigned")) comparator_2 (
    .a(TOP_PTR_q), .b({5{1'b0}}), .eq(HAS_NEXT));  // open: gt, lt
  Multiplexer #(.select(5), .width(16), .enable("false")) multiplexer_2 (
    .in0(sut4_1_out_1), .in1(sut4_1_out_2), .in2(sut4_1_out_3), .in3(sut4_1_out_4), .in4(sut4_1_out_5),
    .in5(sut4_1_out_6), .in6(sut4_1_out_7), .in7(sut4_1_out_8), .in8(sut4_1_out_9), .in9(sut4_1_out_10),
    .in10(sut4_1_out_11), .in11(sut4_1_out_12), .in12(sut4_1_out_13), .in13(sut4_1_out_14),
    .in14(sut4_1_out_15), .in15(sut4_1_out_16), .in16(_1), .in17(sut4_2_out_2), .in18(sut4_2_out_3),
    .in19(sut4_2_out_4), .in20(sut4_2_out_5), .in21(sut4_2_out_6), .in22(sut4_2_out_7), .in23(sut4_2_out_8),
    .in24(sut4_2_out_9), .in25(sut4_2_out_10), .in26(sut4_2_out_11), .in27(sut4_2_out_11),
    .in28(sut4_2_out_13), .in29(sut4_2_out_14), .in30(sut4_2_out_15), .in31(sut4_2_out_16), .out(NEXT),
    .sel(subtractor_4_out));
  Subtractor #(.width(5)) subtractor_4 (.a(TOP_PTR_q), .b(5'b00010), .out(subtractor_4_out));  // open: bin, bout
  Multiplexer #(.select(5), .width(16), .enable("false")) multiplexer_3 (
    .in0(sut4_1_out_1), .in1(sut4_1_out_2), .in2(sut4_1_out_3), .in3(sut4_1_out_4), .in4(sut4_1_out_5),
    .in5(sut4_1_out_6), .in6(sut4_1_out_7), .in7(sut4_1_out_8), .in8(sut4_1_out_9), .in9(sut4_1_out_10),
    .in10(sut4_1_out_11), .in11(sut4_1_out_12), .in12(sut4_1_out_13), .in13(sut4_1_out_14),
    .in14(sut4_1_out_15), .in15(sut4_1_out_16), .in16(_1), .in17(sut4_2_out_2), .in18(sut4_2_out_3),
    .in19(sut4_2_out_4), .in20(sut4_2_out_5), .in21(sut4_2_out_6), .in22(sut4_2_out_7), .in23(sut4_2_out_8),
    .in24(sut4_2_out_9), .in25(sut4_2_out_10), .in26(sut4_2_out_11), .in27(sut4_2_out_11),
    .in28(sut4_2_out_13), .in29(sut4_2_out_14), .in30(sut4_2_out_15), .in31(sut4_2_out_16), .out(TOP),
    .sel(subtractor_5_out));
  Subtractor #(.width(5)) subtractor_5 (.a(TOP_PTR_q), .b(5'b00001), .out(subtractor_5_out));  // open: bin, bout
endmodule

module sut1 (
  input  [15:0] NEXT,
  input  [15:0] IN,
  input  [15:0] TOP,
  input  IS_NEXT,
  input  SWAP,
  output [15:0] OUT
);

  wire [15:0] multiplexer_1_out;

  Multiplexer #(.width(16), .enable("false")) multiplexer_1 (
    .in0(NEXT), .in1(TOP), .out(multiplexer_1_out), .sel(IS_NEXT));
  Multiplexer #(.width(16), .enable("false")) multiplexer_2 (.in0(IN), .in1(multiplexer_1_out), .out(OUT), .sel(SWAP));
endmodule

module sut2 (
  input  [15:0] NEXT,
  input  [15:0] TOP,
  input  [15:0] IN,
  input  SWAP,
  input  IS_NEXT,
  input  CLOCK,
  input  SEL,
  input  EN,
  input  [15:0] in_9,
  input  in_10,
  output [15:0] out_11,
  output [15:0] OUT
);

  wire and_1_out, and_2_out, d_ff_1_q, d_ff_1_qn, decoder_1_out0, decoder_1_out1, or_1_out;
  wire [15:0] multiplexer_1_out, multiplexer_2_out, register_2_q, register_3_q;

  Decoder #(.enable("false")) decoder_1 (.out0(decoder_1_out0), .out1(decoder_1_out1), .sel(d_ff_1_q));
  and and_1 (and_1_out, CLOCK, in_10);
  Multiplexer #(.width(16), .enable("false")) multiplexer_1 (
    .in0(NEXT), .in1(TOP), .out(multiplexer_1_out), .sel(IS_NEXT));
  Multiplexer #(.width(16), .enable("false")) multiplexer_2 (
    .in0(IN), .in1(multiplexer_1_out), .out(multiplexer_2_out), .sel(SWAP));
  and and_2 (and_2_out, IS_NEXT, SWAP);
  or or_1 (or_1_out, EN, and_2_out);
  D_Flip_Flop d_ff_1 (.clk(and_1_out), .D(d_ff_1_qn), .Q(d_ff_1_q), .Qn(d_ff_1_qn));  // open: preset, reset
  Register #(.width(16), .Select("low")) register_1 (
    .D(multiplexer_2_out), .en(or_1_out), .Q(OUT), .clk(CLOCK), .cs(SEL));  // open: clr, preset
  Register #(.width(16), .Select("low")) register_2 (
    .D(in_9), .en(decoder_1_out0), .Q(register_2_q), .clk(and_1_out));  // open: clr
  Register #(.width(16), .Select("low")) register_3 (
    .D(in_9), .en(decoder_1_out1), .Q(register_3_q), .clk(and_1_out));  // open: clr
  Multiplexer #(.width(16), .enable("false")) multiplexer_3 (
    .in0(register_2_q), .in1(register_3_q), .out(out_11), .sel(d_ff_1_q));
endmodule

module sut3 (
  input  [15:0] NEXT,
  input  [15:0] TOP,
  input  [15:0] IN,
  input  IS_NEXT_1,
  input  SWAP,
  input  EN_1,
  input  CLOCK,
  input  IS_NEXT_2,
  input  SEL,
  input  EN_2,
  input  IS_NEXT_3,
  input  EN_3,
  input  IS_NEXT_4,
  input  EN_4,
  output [15:0] OUT_1,
  output [15:0] OUT_2,
  output [15:0] OUT_3,
  output [15:0] OUT_4
);

  sut2 sut2_1 (
    .NEXT(NEXT), .TOP(TOP), .IN(IN), .SWAP(SWAP), .IS_NEXT(IS_NEXT_1), .CLOCK(CLOCK), .SEL(SEL), .EN(EN_1),
    .OUT(OUT_1));  // open: in_10, out_11, in_9
  sut2 sut2_2 (
    .NEXT(NEXT), .TOP(TOP), .IN(IN), .SWAP(SWAP), .IS_NEXT(IS_NEXT_2), .CLOCK(CLOCK), .SEL(SEL), .EN(EN_2),
    .OUT(OUT_2));  // open: in_10, out_11, in_9
  sut2 sut2_3 (
    .NEXT(NEXT), .TOP(TOP), .IN(IN), .SWAP(SWAP), .IS_NEXT(IS_NEXT_3), .CLOCK(CLOCK), .SEL(SEL), .EN(EN_3),
    .OUT(OUT_3));  // open: in_10, out_11, in_9
  sut2 sut2_4 (
    .NEXT(NEXT), .TOP(TOP), .IN(IN), .SWAP(SWAP), .IS_NEXT(IS_NEXT_4), .CLOCK(CLOCK), .SEL(SEL), .EN(EN_4),
    .OUT(OUT_4));  // open: in_10, out_11, in_9
endmodule

module sut4 (
  input  [15:0] NEXT,
  input  [15:0] TOP,
  input  IS_NEXT_1,
  input  EN_1,
  input  IS_NEXT_2,
  input  [15:0] IN,
  input  EN_2,
  input  IS_NEXT_3,
  input  EN_3,
  input  IS_NEXT_4,
  input  EN_4,
  input  SWAP,
  input  CLOCK,
  input  IS_NEXT_5,
  input  EN_5,
  input  IS_NEXT_6,
  input  SEL,
  input  EN_6,
  input  IS_NEXT_7,
  input  EN_7,
  input  IS_NEXT_8,
  input  EN_8,
  input  IS_NEXT_9,
  input  EN_9,
  input  IS_NEXT_10,
  input  EN_10,
  input  IS_NEXT_11,
  input  EN_11,
  input  IS_NEXT_12,
  input  EN_12,
  input  IS_NEXT_13,
  input  EN_13,
  input  IS_NEXT_14,
  input  EN_14,
  input  IS_NEXT_15,
  input  EN_15,
  input  IS_NEXT_16,
  input  EN_16,
  output [15:0] OUT_1,
  output [15:0] OUT_2,
  output [15:0] OUT_3,
  output [15:0] OUT_4,
  output [15:0] OUT_5,
  output [15:0] OUT_6,
  output [15:0] OUT_7,
  output [15:0] OUT_8,
  output [15:0] OUT_9,
  output [15:0] OUT_10,
  output [15:0] OUT_11,
  output [15:0] OUT_12,
  output [15:0] OUT_13,
  output [15:0] OUT_14,
  output [15:0] OUT_15,
  output [15:0] OUT_16
);

  sut3 sut3_1 (
    .NEXT(NEXT), .TOP(TOP), .IN(IN), .IS_NEXT_1(IS_NEXT_1), .SWAP(SWAP), .EN_1(EN_1), .CLOCK(CLOCK),
    .IS_NEXT_2(IS_NEXT_2), .SEL(SEL), .EN_2(EN_2), .IS_NEXT_3(EN_3), .EN_3(EN_3), .IS_NEXT_4(IS_NEXT_4),
    .EN_4(EN_4), .OUT_1(OUT_1), .OUT_2(OUT_2), .OUT_3(OUT_3), .OUT_4(OUT_4));
  sut3 sut3_2 (
    .NEXT(NEXT), .TOP(TOP), .IN(IN), .IS_NEXT_1(IS_NEXT_5), .SWAP(SWAP), .EN_1(EN_5), .CLOCK(CLOCK),
    .IS_NEXT_2(IS_NEXT_6), .SEL(SEL), .EN_2(EN_6), .IS_NEXT_3(IS_NEXT_7), .EN_3(EN_7), .IS_NEXT_4(IS_NEXT_8),
    .EN_4(EN_8), .OUT_1(OUT_5), .OUT_2(OUT_6), .OUT_3(OUT_7), .OUT_4(OUT_8));
  sut3 sut3_3 (
    .NEXT(NEXT), .TOP(TOP), .IN(IN), .IS_NEXT_1(IS_NEXT_9), .SWAP(SWAP), .EN_1(EN_9), .CLOCK(CLOCK),
    .IS_NEXT_2(IS_NEXT_10), .SEL(SEL), .EN_2(EN_10), .IS_NEXT_3(IS_NEXT_11), .EN_3(EN_11),
    .IS_NEXT_4(IS_NEXT_12), .EN_4(EN_12), .OUT_1(OUT_9), .OUT_2(OUT_10), .OUT_3(OUT_11), .OUT_4(OUT_12));
  sut3 sut3_4 (
    .NEXT(NEXT), .TOP(TOP), .IN(IN), .IS_NEXT_1(IS_NEXT_13), .SWAP(SWAP), .EN_1(EN_13), .CLOCK(CLOCK),
    .IS_NEXT_2(IS_NEXT_14), .SEL(SEL), .EN_2(EN_14), .IS_NEXT_3(IS_NEXT_15), .EN_3(EN_15),
    .IS_NEXT_4(IS_NEXT_16), .EN_4(EN_16), .OUT_1(OUT_13), .OUT_2(OUT_14), .OUT_3(OUT_15), .OUT_4(OUT_16));

  assign IS_NEXT_3 = EN_3;
endmodule
